# Fritzing sketch LED_Buzzer_Diagram (saved by Fritzing 0.9.3b)
breadboards: 1

parts:
  Raspberry_Pi_1 = Raspberry Pi 3 [part_number=RPI-3-V1.2]
  LED1 = smd LED [color="Red (633nm)" package="1206 [SMD]"]
  LED2 = smd LED [color="Blue (430nm)" package="1206 [SMD]"]
  R1 = Resistor [tolerance=±5% resistance=330 package="2512 [SMD]"]
  R2 = Resistor [tolerance=±5% resistance=330 package="2512 [SMD]"]
  J1 = Piezo Speaker

nets:
  N1: Raspberry_Pi_1.GPIO22, J1.pin2
  N2: Raspberry_Pi_1.GPIO24, LED2.anode
  N3: Raspberry_Pi_1.GPIO18, LED1.anode
  N4: Raspberry_Pi_1.GND, R1.Pin_0, R2.Pin_0, J1.pin1
  N5: LED1.cathode, R1.Pin_1
  N6: LED2.cathode, R2.Pin_1
